// Logisim project subleq.circ as structural Verilog: 5 circuits, main circuit main
module main (
  input  RST,
  output [23:0] out_2
);

  wire clk, execute, fetch, leqzero;
  wire [7:0] dataC, dual_port_ram_1_data_a, dual_port_ram_1_data_b, multiplexer_1_out, PC,
       pc_increment_1_pcout;
  wire [23:0] rom_1_data;

  Clock clock_1 (.out(clk));
  ROM #(.dataWidth(24)) rom_1 (.addr(PC), .data(rom_1_data), .sel(1'b1));
  Sequencer sequencer_1 (.RST(RST), .Clk(clk), .F(fetch), .E(execute));
  Register #(.width(24)) IR (.D(rom_1_data), .en(fetch), .Q(out_2), .clk(clk), .clr(RST));
  // Probe on fetch
  // Probe on execute
  pc_increment pc_increment_1 (.clk(clk), .fetch(fetch), .pc(PC), .PCout(pc_increment_1_pcout));
  Dual_Port_Ram dual_port_ram_1 (
    .WE(execute), .Addr_A(out_2[23:16]), .Addr_B(out_2[15:8]), .Addr_C(out_2[15:8]), .dataC(dataC),
    .Clk(clk), .Data_A(dual_port_ram_1_data_a), .Data_B(dual_port_ram_1_data_b), .Clr(RST));
  // Probe on dual_port_ram_1_data_a
  // Probe on dual_port_ram_1_data_b
  Multiplexer #(.width(8)) multiplexer_1 (
    .in0(pc_increment_1_pcout), .in1(out_2[7:0]), .out(multiplexer_1_out), .sel(leqzero));
  ALU alu_1 (.A(dual_port_ram_1_data_a), .B(dual_port_ram_1_data_b), .O(dataC), .LEQZERO(leqzero));  // open: CO
  // Probe on dataC
  // Probe on leqzero
  // Probe on PC
  Register u_PC (.D(multiplexer_1_out), .en(execute), .Q(PC), .clk(clk), .clr(RST));

  // Other names for the same wires on the sheet: instr_out[23:0] = out_2

  // Notes on the sheet:
  //   Rom
  //   contents of rom_1 (hex, n*v repeats v):
  //   1 12 3 2 1 0 3 2 1 32 32 32
endmodule

module ALU (
  input  [7:0] A,
  input  [7:0] B,
  output [7:0] O,
  output LEQZERO,
  output CO
);

  wire bitselector_1_out, comparator_1_eq;
  wire [7:0] not_1_out;

  assign not_1_out = ~B;  // NOT_Gate not_1, 8 bits wide
  Adder adder_1 (.a(A), .b(not_1_out), .out(O), .cin(1'b1), .cout(CO));
  Comparator comparator_1 (.a(O), .b({8{1'b0}}), .eq(comparator_1_eq));  // open: gt, lt
  BitSelector bitselector_1 (.in(O), .out(bitselector_1_out), .sel(3'b111));
  or or_1 (LEQZERO, comparator_1_eq, bitselector_1_out);

  // Notes on the sheet:
  //   ALU
endmodule

module Dual_Port_Ram (
  input  WE,
  input  [7:0] Addr_A,
  input  [7:0] Addr_B,
  input  [7:0] Addr_C,
  input  [7:0] dataC,
  input  Clk,
  input  Clr,
  output [7:0] Data_A,
  output [7:0] Data_B
);

  wire [7:0] multiplexer_1_out, multiplexer_2_out, ram_1_data, ram_2_data;

  Multiplexer #(.width(8)) multiplexer_1 (.in0(Addr_A), .in1(Addr_C), .out(multiplexer_1_out), .sel(WE));
  Multiplexer #(.width(8)) multiplexer_2 (.in0(Addr_B), .in1(Addr_C), .out(multiplexer_2_out), .sel(WE));
  RAM #(.bus("separate")) ram_1 (
    .addr(multiplexer_1_out), .din(dataC), .data(ram_1_data), .str(WE), .sel(1'b1), .clk(Clk), .ld(1'b1),
    .clr(Clr));
  RAM #(.bus("separate")) ram_2 (
    .addr(multiplexer_2_out), .din(dataC), .data(ram_2_data), .str(WE), .sel(1'b1), .clk(Clk), .ld(1'b1),
    .clr(Clr));
  Register register_1 (.D(ram_1_data), .en(1'b1), .Q(Data_A), .clk(Clk), .clr(Clr));
  Register register_2 (.D(ram_2_data), .en(1'b1), .Q(Data_B), .clk(Clk), .clr(Clr));

  // Notes on the sheet:
  //   Dual Port Ram
endmodule

module Sequencer (
  input  RST,
  input  Clk,
  output F,
  output E
);

  wire and_1_out, q1;

  and and_1 (and_1_out, ~RST, ~q1);  // AND_Gate
  D_Flip_Flop d_ff_1 (.clk(Clk), .D(and_1_out), .Q(q1), .en(1'b1), .reset(RST));  // open: Qn, preset
  not not_1 (F, q1);
  buf buffer_1 (E, q1);
endmodule

module pc_increment (
  input  clk,
  input  fetch,
  input  [7:0] pc,
  output [7:0] PCout
);

  wire [7:0] adder_1_out;

  Adder adder_1 (.a(pc), .b(8'h1), .out(adder_1_out));  // open: cin, cout
  Register register_1 (.D(adder_1_out), .en(fetch), .Q(PCout), .clk(clk));  // open: clr
endmodule
